// Logisim project selective_pwm_3bit.circ as structural Verilog: 1 circuit, main circuit main
module main (
);

  wire clock_1_out, comparator_1_gt, digital_oscilloscope_1_p2, dipswitch_1_p1, dipswitch_1_p3,
       dipswitch_1_p5, dipswitch_1_p6, dipswitch_1_p7, dipswitch_2_p1, dipswitch_2_p2, dipswitch_2_p4,
       dipswitch_2_p6;
  wire [2:0] counter_1_q, priority_encoder_1_p3, register_1_q;

  // DipSwitch #(.number(1)) dipswitch_1: pin names not known; wires that end beside it: dipswitch_1_p1, dipswitch_1_p1, dipswitch_1_p3, dipswitch_1_p3, dipswitch_1_p5, dipswitch_1_p6, dipswitch_1_p7
  Clock clock_1 (.out(clock_1_out));
  // DipSwitch dipswitch_2: pin names not known; wires that end beside it: dipswitch_2_p1, dipswitch_2_p2, dipswitch_2_p2, dipswitch_2_p4, dipswitch_2_p4, dipswitch_2_p6
  // Priority_Encoder priority_encoder_1: pin names not known; wires that end beside it: dipswitch_1_p5, dipswitch_1_p6, priority_encoder_1_p3, dipswitch_1_p7, dipswitch_2_p1
  Register #(.trigger("high"), .width(3)) register_1 (
    .D(priority_encoder_1_p3), .Q(register_1_q), .clk(clock_1_out));  // open: en, clr
  Counter #(.max('h7), .width(3)) counter_1 (
    .load(1'b0), .count(1'b1), .Q(counter_1_q), .up(1'b1), .clk(clock_1_out));  // open: D, carry, clr
  Comparator #(.mode("unsigned"), .width(3)) comparator_1 (
    .a(register_1_q), .b(counter_1_q), .gt(comparator_1_gt));  // open: eq, lt
  // Digital_Oscilloscope #(.nState(16), .showclock("false")) digital_oscilloscope_1: pin names not known; wires that end beside it: clock_1_out, digital_oscilloscope_1_p2
  or or_1 (digital_oscilloscope_1_p2, dipswitch_2_p6, comparator_1_gt);
endmodule
